// Logisim project Project2.circ as structural Verilog: 9 circuits, main circuit Register File
module main (
  input  Reset
);

  wire Clock_out, Decoder_branch, Decoder_halt, Decoder_memread, Decoder_memwrite, Decoder_regdst,
       Decoder_regwrite, demultiplexer_1_out1, demultiplexer_2_out1, not_1_p1, not_1_p2, not_2_p1, not_2_p2,
       not_3_out;
  wire [1:0] Decoder_alusrc, Decoder_jump, Decoder_memtoreg;
  wire [2:0] Decoder_aluop, Extracting_Instruction_rs, Extracting_Instruction_rt, multiplexer_4_out;
  wire [3:0] put_1_led0, put_1_led1, put_1_led3;
  wire [4:0] Extracting_Instruction_opcode;
  wire [7:0] adder_1_out, bit_extender_1_out, Extracting_Instruction_imm, multiplexer_1_out,
       multiplexer_2_out, multiplexer_3_out, PC_q, Register_File_readdata1;
  wire [15:0] ALU_result, bit_extender_2_out, bit_extender_3_out, bit_extender_4_out, bit_extender_5_out,
       multiplexer_5_out, multiplexer_6_out, multiplexer_7_out, Multiplier_and_Divider_result1,
       Multiplier_and_Divider_result2, ram_1_data, Register_File_readdata2, rom_1_data;
  wire [15:8] Register_File_readdata1_2;

  // NOT_Gate not_1: pin names not known; wires that end beside it: not_1_p1, not_1_p2
  Multiplexer #(.width(8)) multiplexer_1 (
    .in0(multiplexer_2_out), .in1({8{1'b0}}), .out(multiplexer_1_out), .sel(Reset));  // open: en
  Clock Clock (.out(Clock_out));
  assign bit_extender_1_out = {{7{1'b0}}, 1'b1};  // Bit_Extender bit_extender_1
  Register PC (.D(multiplexer_1_out), .en(not_1_p2), .Q(PC_q), .clk(Clock_out));  // open: clr
  Multiplexer #(.width(8)) multiplexer_2 (
    .in0({8{1'b0}}), .in1(multiplexer_3_out), .out(multiplexer_2_out), .sel(Decoder_branch));  // open: en
  Adder adder_1 (.a(bit_extender_1_out), .b(PC_q), .out(adder_1_out));  // open: cin, cout
  Multiplexer #(.select(2), .width(8)) multiplexer_3 (
    .in0(adder_1_out), .in1(Extracting_Instruction_imm), .in2(Register_File_readdata1),
    .out(multiplexer_3_out), .sel(Decoder_jump));  // open: in3, en
  ROM #(.dataWidth(16)) rom_1 (.addr(PC_q), .data(rom_1_data));  // open: sel
  // NOT_Gate not_2: pin names not known; wires that end beside it: not_2_p1, not_2_p2
  Demultiplexer demultiplexer_1 (
    .out0(not_1_p1), .out1(demultiplexer_1_out1), .in(Decoder_halt), .sel(not_2_p1));  // open: en
  Decoder2 Decoder (
    .OpCodeAndSubOp(Extracting_Instruction_opcode), .Jump(Decoder_jump), .Halt(Decoder_halt),
    .RegDst(Decoder_regdst), .Branch(Decoder_branch), .MemRead(Decoder_memread),
    .MemToReg(Decoder_memtoreg[0]), .ALUOp(Decoder_aluop), .MemWrite(Decoder_memwrite),
    .ALUSrc(Decoder_alusrc), .RegWrite(Decoder_regwrite), .RegWrite_2(Decoder_regwrite));
  Extracting_Instruction Extracting_Instruction (
    .Instruction(rom_1_data), .Subop(not_2_p2), .Imm(Extracting_Instruction_imm),
    .Rt(Extracting_Instruction_rt), .Rs(Extracting_Instruction_rs), .Opcode(Extracting_Instruction_opcode));
  LED led_1 (.in(not_1_p1));
  Multiplexer #(.width(3)) multiplexer_4 (
    .in0(Extracting_Instruction_rs), .in1(Extracting_Instruction_rt), .out(multiplexer_4_out),
    .sel(Decoder_regdst));  // open: en
  Hex_Digit_Display hex_digit_display_1 (.value(put_1_led3));  // open: dp
  assign bit_extender_2_out = {{8{1'b0}}, adder_1_out};  // Bit_Extender bit_extender_2
  Register2 Register_File (
    .EnableWrite(Decoder_regwrite), .EnableWrite2(Decoder_memwrite),
    .ReadRegister1(Extracting_Instruction_rs), .ReadRegister2(Extracting_Instruction_rt),
    .WriteRegister(multiplexer_4_out), .WriteData1(multiplexer_7_out),
    .WriteData2(Multiplier_and_Divider_result2), .Clock(Clock_out),
    .ReadData1({Register_File_readdata1_2, Register_File_readdata1}), .ReadData2(Register_File_readdata2));
  assign bit_extender_3_out = {{8{Extracting_Instruction_imm[7]}}, Extracting_Instruction_imm};  // Bit_Extender bit_extender_3
  assign bit_extender_4_out = {{8{1'b0}}, Extracting_Instruction_imm};  // Bit_Extender bit_extender_4
  assign bit_extender_5_out = {{15{1'b0}}, 1'b0};  // Bit_Extender bit_extender_5
  Hex_Digit_Display hex_digit_display_2 (.value(put_1_led1));  // open: dp
  Hex_Digit_Display hex_digit_display_3 (.value(put_1_led3));  // open: dp
  Put put_1 (
    .Print({Register_File_readdata1_2, Register_File_readdata1}), .LED3(put_1_led3), .LED2(put_1_led3),
    .LED1(put_1_led1), .LED0(put_1_led0), .EnablePut(not_3_out), .Clock(Clock_out));
  not not_3 (not_3_out, demultiplexer_1_out1);
  Hex_Digit_Display hex_digit_display_4 (.value(put_1_led0));  // open: dp
  Multiplexer #(.select(2), .width(16)) multiplexer_5 (
    .in0({Register_File_readdata1_2, Register_File_readdata1}), .in1(bit_extender_2_out),
    .in2(bit_extender_5_out), .out(multiplexer_5_out), .sel(Decoder_alusrc));  // open: in3, en
  Multiplexer #(.select(2), .width(16)) multiplexer_6 (
    .in0(Register_File_readdata2), .in1(bit_extender_3_out), .in2(bit_extender_4_out),
    .in3(bit_extender_5_out), .out(multiplexer_6_out), .sel(Decoder_alusrc), .en(Decoder_alusrc[0]));
  ALU ALU (.A(multiplexer_5_out), .B(multiplexer_6_out), .Opcode(Decoder_aluop), .Subop(not_2_p2), .Result(ALU_result));
  Multiplier_and_Divider Multiplier_and_Divider (
    .A({Register_File_readdata1_2, Register_File_readdata1}), .B(Register_File_readdata2), .Subop(not_2_p2),
    .Result1(Multiplier_and_Divider_result1), .Result2(Multiplier_and_Divider_result2));
  Multiplexer #(.select(2), .width(16)) multiplexer_7 (
    .in0(ALU_result), .in1(Multiplier_and_Divider_result1), .in2(ram_1_data), .out(multiplexer_7_out),
    .sel(Decoder_memtoreg));  // open: in3, en
  RAM #(.dataWidth(16), .bus("separate")) ram_1 (
    .addr(Register_File_readdata2[7:0]), .din({Register_File_readdata1_2, Register_File_readdata1}),
    .data(ram_1_data), .str(demultiplexer_2_out1), .ld(Decoder_memtoreg[1]));  // open: sel, clk, clr
  Demultiplexer demultiplexer_2 (
    .out0(Decoder_memtoreg[1]), .out1(demultiplexer_2_out1), .in(Decoder_memread), .sel(not_2_p2));  // open: en
  // Pins of 1 and 2 bits meet at Decoder_alusrc

  // Notes on the sheet:
  //   Instruction Memory
  //   contents of rom_1 (hex, n*v repeats v):
  //   9200 7200 8203 1481 1400 85e1 a403 6000
  //   Data Memory
endmodule

module Register_File (
  input  WriteEnable,
  input  [1:0] ReadRegister1,
  input  [1:0] ReadRegister2,
  input  [1:0] WriteRegister,
  input  [15:0] WriteData,
  input  Clock,
  output [15:0] ReadData1,
  output [15:0] ReadData2
);

  wire and_1_out, and_2_out, and_3_out, and_4_out, decoder_1_out0, decoder_1_out1, decoder_1_out2,
       decoder_1_out3;
  wire [15:0] register_1_q, register_2_q, register_3_q, register_4_q, undriven;

  Decoder #(.select(2)) decoder_1 (
    .out0(decoder_1_out0), .out1(decoder_1_out1), .out2(decoder_1_out2), .out3(decoder_1_out3),
    .sel(WriteRegister));  // open: en
  and and_1 (and_1_out, decoder_1_out0, WriteEnable);
  and and_2 (and_2_out, decoder_1_out1, WriteEnable);
  and and_3 (and_3_out, decoder_1_out2, WriteEnable);
  and and_4 (and_4_out, decoder_1_out3, WriteEnable);
  Register #(.width(16)) register_1 (.D(undriven), .en(and_1_out), .Q(register_1_q), .clk(Clock));  // open: clr
  Register #(.width(16)) register_2 (.D(undriven), .en(and_2_out), .Q(register_2_q), .clk(Clock));  // open: clr
  Register #(.width(16)) register_3 (.D(undriven), .en(and_3_out), .Q(register_3_q), .clk(Clock));  // open: clr
  Register #(.width(16)) register_4 (.D(undriven), .en(and_4_out), .Q(register_4_q), .clk(Clock));  // open: clr
  // Multiplexer #(.select(2), .width(16)) multiplexer_1: pin names not known; wires that end beside it: register_1_q, register_2_q, register_3_q, register_4_q, ReadRegister1, ReadData1
  // Multiplexer #(.select(2), .width(16)) multiplexer_2: pin names not known; wires that end beside it: register_1_q, register_2_q, register_3_q, register_4_q, ReadRegister2, ReadData2
endmodule

module Extracting_Instruction (
  input  [15:0] Instruction,
  output Subop,
  output [7:0] Imm,
  output [2:0] Rt,
  output [2:0] Rs,
  output [4:0] Opcode
);


  assign Imm = Instruction[8:1];
  assign Opcode = {Instruction[15:12], Instruction[0]};
  assign Rs = Instruction[11:9];
  assign Rt = Instruction[8:6];
  assign Subop = Instruction[0];
endmodule

module ALU (
  input  Subop,
  input  [2:0] Opcode,
  input  [15:0] A,
  input  [15:0] B,
  output [15:0] Result
);

  wire comparator_1_gt, comparator_1_lt, not_1_p1, not_1_p2;
  wire [15:0] adder_1_out, and_1_out, bit_extender_1_out, bit_extender_2_out, bit_extender_3_out,
       bit_extender_4_out, multiplexer_1_out, multiplexer_2_p4, multiplexer_3_p4, multiplexer_4_p4,
       multiplexer_5_out, nor_1_out, shifter_1_out, shifter_2_out, subtractor_1_out;

  assign and_1_out = A & B;  // AND_Gate and_1, 16 bits wide
  assign nor_1_out = ~(A | B);  // NOR_Gate nor_1, 16 bits wide
  Adder #(.width(16)) adder_1 (.a(A), .b(B), .out(adder_1_out));  // open: cin, cout
  Subtractor #(.width(16)) subtractor_1 (.a(A), .b(B), .out(subtractor_1_out));  // open: bin, bout
  Shifter #(.width(16)) shifter_1 (.in(A), .\dist (B[3:0]), .out(shifter_1_out));
  Shifter #(.width(16), .shift("lr")) shifter_2 (.in(A), .\dist (B[3:0]), .out(shifter_2_out));
  // NOT_Gate not_1: pin names not known; wires that end beside it: not_1_p1, not_1_p2
  Comparator #(.width(16)) comparator_1 (.a(A), .b(B), .gt(comparator_1_gt), .eq(not_1_p2), .lt(comparator_1_lt));
  Multiplexer #(.width(16)) multiplexer_1 (
    .in0(and_1_out), .in1(nor_1_out), .out(multiplexer_1_out), .sel(Subop));  // open: en
  // Multiplexer #(.width(16)) multiplexer_2: pin names not known; wires that end beside it: adder_1_out, subtractor_1_out, Subop, multiplexer_2_p4
  // Multiplexer #(.width(16)) multiplexer_3: pin names not known; wires that end beside it: shifter_1_out, shifter_2_out, Subop, multiplexer_3_p4
  assign bit_extender_1_out = {{15{1'b0}}, not_1_p1};  // Bit_Extender bit_extender_1
  assign bit_extender_2_out = {{15{1'b0}}, not_1_p2};  // Bit_Extender bit_extender_2
  assign bit_extender_3_out = {{15{1'b0}}, comparator_1_gt};  // Bit_Extender bit_extender_3
  assign bit_extender_4_out = {{15{1'b0}}, comparator_1_lt};  // Bit_Extender bit_extender_4
  // Multiplexer #(.width(16)) multiplexer_4: pin names not known; wires that end beside it: bit_extender_1_out, bit_extender_2_out, Subop, multiplexer_4_p4
  Multiplexer #(.width(16)) multiplexer_5 (
    .in0(bit_extender_3_out), .in1(bit_extender_4_out), .out(multiplexer_5_out), .sel(Subop));  // open: en
  Multiplexer #(.select(3), .width(16)) multiplexer_6 (
    .in0(multiplexer_1_out), .in1(adder_1_out), .in2(multiplexer_2_p4), .in3(multiplexer_3_p4),
    .in4(multiplexer_4_p4), .in5(multiplexer_5_out), .in6(multiplexer_5_out), .in7(multiplexer_5_out),
    .out(Result), .sel(Opcode));  // open: en
endmodule

module Register2 (
  input  EnableWrite,
  input  EnableWrite2,
  input  [2:0] ReadRegister1,
  input  [2:0] ReadRegister2,
  input  [2:0] WriteRegister,
  input  [15:0] WriteData1,
  input  [15:0] WriteData2,
  input  Clock,
  output [15:0] ReadData1,
  output [15:0] ReadData2
);

  wire demultiplexer_1_p3, demultiplexer_1_p4, demultiplexer_1_p5, demultiplexer_1_p6, demultiplexer_1_p7,
       demultiplexer_1_p8, demultiplexer_1_p9, demultiplexer_1_p10, \do ;
  wire [2:0] bit_extender_1_out;
  wire [15:0] multiplexer_1_out, multiplexer_2_out, multiplexer_3_out, multiplexer_4_out, multiplexer_5_out,
       multiplexer_6_out, multiplexer_7_out, multiplexer_8_out, r0, r1, r2, r3, r4, r5, r6, r7;

  assign bit_extender_1_out = {{2{1'b0}}, 1'b1};  // Bit_Extender bit_extender_1
  Adder #(.width(3)) adder_1 (.b(bit_extender_1_out), .out(WriteRegister));  // open: a, cin, cout
  or or_1 (\do , EnableWrite, EnableWrite2);
  // Demultiplexer #(.select(3)) demultiplexer_1: pin names not known; wires that end beside it: EnableWrite2, WriteRegister, demultiplexer_1_p3, demultiplexer_1_p4, demultiplexer_1_p5, demultiplexer_1_p6, demultiplexer_1_p7, demultiplexer_1_p8, demultiplexer_1_p9, demultiplexer_1_p10
  Multiplexer #(.width(16)) multiplexer_1 (
    .in0(WriteData1), .in1(WriteData2), .out(multiplexer_1_out), .sel(demultiplexer_1_p3));  // open: en
  Multiplexer #(.width(16)) multiplexer_2 (
    .in0(WriteData1), .in1(WriteData2), .out(multiplexer_2_out), .sel(demultiplexer_1_p6));  // open: en
  Multiplexer #(.width(16)) multiplexer_3 (
    .in0(WriteData1), .in1(WriteData2), .out(multiplexer_3_out), .sel(demultiplexer_1_p7));  // open: en
  Multiplexer #(.width(16)) multiplexer_4 (
    .in0(WriteData2), .in1(WriteData2), .out(multiplexer_4_out), .sel(demultiplexer_1_p8));  // open: en
  Multiplexer #(.width(16)) multiplexer_5 (
    .in0(WriteData1), .in1(WriteData2), .out(multiplexer_5_out), .sel(demultiplexer_1_p9));  // open: en
  Multiplexer #(.width(16)) multiplexer_6 (
    .in0(WriteData1), .in1(WriteData2), .out(multiplexer_6_out), .sel(demultiplexer_1_p10));  // open: en
  Multiplexer #(.width(16)) multiplexer_7 (
    .in0(WriteData1), .in1(WriteData2), .out(multiplexer_7_out), .sel(demultiplexer_1_p4));  // open: en
  Multiplexer #(.width(16)) multiplexer_8 (
    .in0(WriteData1), .in1(WriteData2), .out(multiplexer_8_out), .sel(demultiplexer_1_p5));  // open: en
  Register #(.width(16)) s0 (.D(multiplexer_1_out), .en(\do ), .Q(r0), .clk(Clock));  // open: clr
  Register #(.width(16)) s1 (.D(multiplexer_7_out), .en(\do ), .Q(r1), .clk(Clock));  // open: clr
  Register #(.width(16)) s2 (.D(multiplexer_8_out), .en(\do ), .Q(r2), .clk(Clock));  // open: clr
  Register #(.width(16)) s3 (.D(multiplexer_2_out), .en(\do ), .Q(r3), .clk(Clock));  // open: clr
  Register #(.width(16)) s4 (.D(multiplexer_3_out), .en(\do ), .Q(r4), .clk(Clock));  // open: clr
  Register #(.width(16)) s5 (.D(multiplexer_4_out), .en(\do ), .Q(r5), .clk(Clock));  // open: clr
  Register #(.width(16)) s6 (.D(multiplexer_5_out), .en(\do ), .Q(r6), .clk(Clock));  // open: clr
  Register #(.width(16)) s7 (.D(multiplexer_6_out), .en(\do ), .Q(r7), .clk(Clock));  // open: clr
  Multiplexer #(.select(3), .width(16)) multiplexer_9 (
    .in0(r0), .in1(r1), .in2(r2), .in3(r3), .in4(r4), .in5(r5), .in6(r6), .in7(r7), .out(ReadData1),
    .sel(ReadRegister1));  // open: en
  Multiplexer #(.select(3), .width(16)) multiplexer_10 (
    .in0(r0), .in1(r1), .in2(r2), .in3(r3), .in4(r4), .in5(r5), .in6(r6), .in7(r7), .out(ReadData2),
    .sel(ReadRegister2));  // open: en

  // Other names for the same wires on the sheet: read1[2:0] = ReadRegister1; read2[2:0] = ReadRegister2;
  //   write[15:0] = WriteData1; write2[15:0] = WriteData2
endmodule

module Multiplier_and_Divider (
  input  Subop,
  input  [15:0] A,
  input  [15:0] B,
  output [15:0] Result1,
  output [15:0] Result2
);

  wire [15:0] divider_1_out, divider_1_rem, multiplier_1_cout, multiplier_1_out;

  Multiplier #(.width(16)) multiplier_1 (.a(A), .b(B), .out(multiplier_1_out), .cout(multiplier_1_cout));  // open: cin
  Divider #(.width(16)) divider_1 (.a(A), .b(B), .out(divider_1_out), .rem(divider_1_rem));  // open: upper
  Multiplexer #(.width(16)) multiplexer_1 (
    .in0(divider_1_out), .in1(multiplier_1_out), .out(Result1), .sel(Subop));  // open: en
  Multiplexer #(.width(16)) multiplexer_2 (
    .in0(divider_1_rem), .in1(multiplier_1_cout), .out(Result2), .sel(Subop));  // open: en
endmodule

module Put (
  input  [15:0] Print,
  input  EnablePut,
  input  Clock,
  output [3:0] LED3,
  output [3:0] LED2,
  output [3:0] LED1,
  output [3:0] LED0
);

  wire and_1_p2;

  Multiplexer #(.width(16)) multiplexer_1 (
    .in1(Print), .out({LED3, LED2, LED1, LED0}), .sel(and_1_p2), .en(and_1_p2));  // open: in0
  // AND_Gate and_1: pin names not known; wires that end beside it: EnablePut, and_1_p2, Clock
endmodule

module Decoder2 (
  input  [4:0] OpCodeAndSubOp,
  output Halt,
  output RegDst,
  output Branch,
  output MemRead,
  output MemToReg,
  output [2:0] ALUOp,
  output MemWrite,
  output [1:0] ALUSrc,
  output RegWrite,
  output RegWrite_2,
  output [1:0] Jump
);

  wire ADD, addi, addui, AND, bn, bp, bx, bz, div, j, jal, jr, li, lw, mul, multiplexer_6_out, NOR, not_2_p3,
       not_3_p2, not_4_out, not_5_out, not_6_p3, or_1_out, or_3_out, put, sllv, slrv, SUB, sw;
  wire [1:0] multiplexer_2_out, multiplexer_3_out, multiplexer_4_out;

  Multiplexer #(.width(3)) multiplexer_1 (.in1(3'b001), .out(ALUOp), .sel(or_1_out));  // open: in0, en
  or or_1 (or_1_out, ADD, SUB);
  Decoder #(.select(5)) decoder_1 (
    .out0(AND), .out1(NOR), .out2(ADD), .out3(SUB), .out4(sllv), .out5(slrv), .out6(div), .out7(mul),
    .out8(lw), .out9(sw), .out10(jr), .out11(jr), .out12(Halt), .out13(Halt), .out14(put), .out15(put),
    .out16(addui), .out17(addi), .out18(li), .out19(li), .out20(bp), .out21(bn), .out22(bx), .out23(bz),
    .out24(jal), .out25(jal), .out26(j), .out27(j), .sel(OpCodeAndSubOp));  // open: out28, out29, out30, out31, en
  assign Jump = multiplexer_2_out | multiplexer_3_out | multiplexer_4_out;  // OR_Gate or_2, 2 bits wide
  Multiplexer #(.width(2)) multiplexer_2 (.in0(2'b00), .in1(2'b01), .out(multiplexer_2_out), .sel(j));  // open: en
  Multiplexer #(.width(2)) multiplexer_3 (.in0(2'b00), .in1(2'b10), .out(multiplexer_3_out), .sel(jal));  // open: en
  Multiplexer #(.width(2)) multiplexer_4 (.in0(2'b00), .in1(2'b11), .out(multiplexer_4_out), .sel(jr));  // open: en
  Multiplexer multiplexer_5 (.in0(1'b0), .in1(1'b1), .out(MemToReg), .sel(lw));  // open: en
  // NOT_Gate not_1: pin names not known; wires that end beside it: MemToReg, MemToReg, RegDst
  // NOT_Gate not_2: pin names not known; wires that end beside it: MemToReg, MemToReg, not_2_p3
  // NOT_Gate not_3: pin names not known; wires that end beside it: MemToReg, not_3_p2
  Multiplexer multiplexer_6 (.in0(1'b0), .in1(1'b1), .out(multiplexer_6_out), .sel(sw));  // open: en
  not not_4 (not_4_out, multiplexer_6_out);
  not not_5 (not_5_out, multiplexer_6_out);
  // NOT_Gate not_6: pin names not known; wires that end beside it: multiplexer_6_out, multiplexer_6_out, not_6_p3
  or or_3 (or_3_out, bp, bn, bx, bz);
  or or_4 (Branch, not_3_p2, or_3_out, not_6_p3);
  or or_5 (MemRead, MemToReg, not_5_out);
  or or_6 (MemWrite, not_2_p3, multiplexer_6_out, multiplexer_6_out);
  or or_7 (ALUSrc[1], MemToReg, multiplexer_6_out);
  or or_8 (RegWrite, MemToReg, not_4_out);

  assign ALUSrc[0] = 1'b0;
  assign RegWrite_2 = RegWrite;

  // Other names for the same wires on the sheet: Haltput = Halt
endmodule

module InstructionID (
  input  in_1,
  input  [3:0] in_2,
  output [4:0] out_3
);


  assign out_3 = {in_2, in_1};
endmodule
